# Fritzing sketch Trombino (saved by Fritzing 0.8.5b)
stripboards: 1

parts:
  R1 = Resistor [tolerance=±5% resistance=10k package=THT]
  R2 = Resistor [tolerance=±5% resistance=10k package=THT]
  R3 = Resistor [tolerance=±5% resistance=10k package=THT]
  S1 = Pushbutton [package="[THT]"]
  S2 = Pushbutton [package="[THT]"]
  S3 = Pushbutton [package="[THT]"]
  Part1 = Arduino Uno (Rev3)

nets:
  N1: R1.Pin_0, R2.Pin_0, R3.Pin_0, Part1.GND
  N2: R1.Pin_1, S1.Pin_3, S1.Pin_4, Part1.D4
  N3: R2.Pin_1, S3.Pin_3, S3.Pin_4, Part1.D2
  N4: R3.Pin_1, S2.Pin_3, S2.Pin_4, Part1.D3_PWM
  N5: S1.Pin_1, S1.Pin_2, S2.Pin_1, S2.Pin_2, S3.Pin_1, S3.Pin_2, Part1.5V
